# Fritzing sketch Circuit (saved by Fritzing 0.9.3b)
breadboards: 1

parts:
  元件1 = Arduino Uno (Rev3)
  ld = Photocell (LDR) [package=THT]
  lt = Photocell (LDR) [package=THT]
  rd = Photocell (LDR) [package=THT]
  rt = Photocell (LDR) [package=THT]
  hori = Basic Servo
  vert = Basic Servo
  R3 = Resistor [tolerance=±5% resistance=10k package=THT]
  R0 = Resistor [tolerance=±5% resistance=10k package=THT]
  R2 = Resistor [tolerance=±5% resistance=10k package=THT]
  R1 = Resistor [tolerance=±5% resistance=10k package=THT]

nets:
  N1: 元件1.A0, lt.pin_0, R0.Pin_1
  N2: 元件1.A1, rt.pin_1, R1.Pin_1
  N3: 元件1.A2, ld.pin_0, R2.Pin_1
  N4: 元件1.A3, rd.pin_1, R3.Pin_1
  N5: 元件1.D9_PWM, hori.pulse
  N6: 元件1.D10_PWM/SS, vert.pulse
  GND: 元件1.GND, hori.gnd, vert.gnd, R3.Pin_0, R0.Pin_0, R2.Pin_0, R1.Pin_0
  VCC: 元件1.5V, ld.pin_1, lt.pin_1, rd.pin_0, rt.pin_0, hori.vcc, vert.vcc
